# Fritzing sketch Schema (saved by Fritzing 0.9.2b)

parts:
  LED2 = smd LED [color="Green (555nm)" package="0603 [SMD]"]
  Part3 = Arduino Ethernet Shield (Rev3)
  R1 = Resistor [tolerance=±5% resistance=220 package=THT]
  R2 = Resistor [tolerance=±5% resistance=220 package=THT]
  LED1 = smd LED [color="Red (633nm)" package="0603 [SMD]"]

nets:
  N1: LED2.cathode, Part3.GND, LED1.cathode
  N2: LED2.anode, R2.Pin_0
  N3: Part3.D2, R2.Pin_1
  N4: Part3.PWM_D5, R1.Pin_0
  N5: R1.Pin_1, LED1.anode
