# Fritzing sketch Button (saved by Fritzing 0.9.2b)

parts:
  R1 = Resistor [tolerance=±5% resistance=220 package=THT]
  RE1 = Rotary Encoder [package=THT]
  Part1 = Arduino Uno (Rev3)

nets:
  N1: R1.Pin_0, RE1.EncoderPinB, Part1.D10_PWM/SS
  N2: R1.Pin_1, Part1.5V
  N3: RE1.EncoderPinA, Part1.GND
