# Fritzing sketch Scheme (saved by Fritzing 0.9.2b)

parts:
  Part1 = Arduino Uno (Rev3)
  BAT1 = Battery Holders [package=battery-aa]
  BAT2 = Battery Holders [package=battery-aa]
  BAT3 = Battery Holders [package=battery-aa]
  BAT4 = Battery Holders [package=battery-aa]
  U1 = ESP8266 WiFi Module [part_number=ESP8266]

nets:
  N1: Part1.A0, BAT2.+
  N2: Part1.A1, BAT1.+
  N3: Part1.A2, BAT3.+
  N4: Part1.A3, BAT4.+
  GND: Part1.GND, BAT1.-, BAT2.-, BAT3.-, BAT4.-, U1.GND
  N5: Part1.D2, U1.RXD
  N6: Part1.D3_PWM, U1.TXD
  3V3: Part1.3V3, U1.VCC, U1.CH_PD

custom parts:
  ESP8266 WiFi Module: Generic WiFi Module based on the ESP8266 with onboard PCB antenna and UART communications
